# Fritzing sketch arduino (saved by Fritzing 0.9.4)

parts:
  DHT1 = Humidity and Temperature Sensor DHT11
  Part2 = Arduino Board Ethernet

nets:
  VCC: DHT1.Vcc, Part2.5V
  N1: DHT1.Data-signal, Part2.D2_PWM
  N2: DHT1.GND_2, Part2.GND

custom parts:
  Humidity and Temperature Sensor DHT11: Digital relative humidity & temperature sensor DHT11
