# Fritzing sketch esp32 (saved by Fritzing 0.9.4)
breadboards: 1

parts:
  DHT1 = Humidity and Temperature Sensor DHT11
  U1 = ESP32-38PinWide [part_number=ESP32-38PinWide]

nets:
  N1: DHT1.Vcc, U1.3.3
  N2: DHT1.Data-signal, U1.GPIO4
  N3: DHT1.GND_2, U1.GPIO11

custom parts:
  Humidity and Temperature Sensor DHT11: Digital relative humidity & temperature sensor DHT11
  ESP32-38PinWide: Generic 38-Pin ESP32 with wide format (only access to one side of pins on a breadboard) based on Stephen Lilley's HiLetgo ESP-WROOM-32 ESP32 ESP-32S Development Board.
